// Logisim project comparadores.circ as structural Verilog
module main (
  input  a0,
  input  b0,
  input  a1,
  input  b1,
  input  a2,
  input  b2,
  input  a3,
  input  b3,
  input  a4,
  input  b4,
  input  c2,
  input  d2,
  input  c1,
  input  d1,
  input  c0,
  input  d0,
  input  e0,
  input  f0,
  input  e1,
  input  f1,
  output iguais,
  output maior_que,
  output menor_que
);

  wire and_1_out, and_2_out, and_3_out, and_4_out, and_5_out, and_6_out, and_7_out, and_8_out, not_1_out,
       not_2_out, not_3_out, not_4_out, not_5_out, not_6_out, not_7_out, not_8_out, xnor_1_out, xnor_2_out,
       xnor_3_out, xnor_4_out, xnor_5_out, xnor_6_out, xnor_7_out, xnor_8_out;

  xnor xnor_1 (xnor_1_out, c2, d2);
  and and_1 (and_1_out, xnor_1_out, not_2_out);
  xnor xnor_2 (xnor_2_out, c1, d1);
  and and_2 (and_2_out, xnor_2_out, and_1_out, not_4_out);
  xnor xnor_3 (xnor_3_out, e0, f0);
  not not_1 (not_1_out, d2);
  not not_2 (not_2_out, and_4_out);
  not not_3 (not_3_out, d1);
  not not_4 (not_4_out, and_5_out);
  not not_5 (not_5_out, d0);
  not not_6 (not_6_out, e0);
  not not_7 (not_7_out, and_7_out);
  and and_3 (and_3_out, xnor_3_out, not_7_out);
  not not_8 (not_8_out, e1);
  xnor xnor_4 (xnor_4_out, a0, b0);
  xnor xnor_5 (xnor_5_out, a1, b1);
  xnor xnor_6 (xnor_6_out, a2, b2);
  xnor xnor_7 (xnor_7_out, a3, b3);
  xnor xnor_8 (xnor_8_out, a4, b4);
  and and_4 (and_4_out, c2, not_1_out);
  and and_5 (and_5_out, and_1_out, c1, not_3_out);
  and and_6 (and_6_out, and_2_out, c0, not_5_out);
  and and_7 (and_7_out, not_6_out, f0);
  and and_8 (and_8_out, and_3_out, not_8_out, f1);
  or or_1 (maior_que, and_4_out, and_5_out, and_6_out);
  or or_2 (menor_que, and_7_out, and_8_out);
  and and_9 (iguais, xnor_4_out, xnor_5_out, xnor_6_out, xnor_7_out, xnor_8_out);
endmodule

module comparador1bit (
  input  deve_comparar,
  input  a0,
  input  d0,
  output maior_que,
  output nao_tem_resposta
);

  wire not_1_out, xnor_1_out;

  xnor xnor_1 (xnor_1_out, a0, d0);
  and and_1 (nao_tem_resposta, xnor_1_out, deve_comparar);
  not not_1 (not_1_out, d0);
  and and_2 (maior_que, deve_comparar, a0, not_1_out);
endmodule

module comparador_4_bits (
  input  a3,
  input  b3,
  input  a2,
  input  b2,
  input  a1,
  input  b1,
  input  a0,
  input  b0,
  output maior_que
);

  wire comparador1bit_1_maior_que, comparador1bit_1_nao_tem_resposta, comparador1bit_2_maior_que,
       comparador1bit_2_nao_tem_resposta, comparador1bit_3_maior_que, comparador1bit_3_nao_tem_resposta,
       comparador1bit_4_maior_que;

  comparador1bit comparador1bit_1 (
    .deve_comparar(1'b1), .a0(a3), .d0(b3), .maior_que(comparador1bit_1_maior_que),
    .nao_tem_resposta(comparador1bit_1_nao_tem_resposta));
  comparador1bit comparador1bit_2 (
    .deve_comparar(comparador1bit_1_nao_tem_resposta), .a0(a2), .d0(b2),
    .maior_que(comparador1bit_2_maior_que), .nao_tem_resposta(comparador1bit_2_nao_tem_resposta));
  comparador1bit comparador1bit_3 (
    .deve_comparar(comparador1bit_2_nao_tem_resposta), .a0(a1), .d0(b1),
    .maior_que(comparador1bit_3_maior_que), .nao_tem_resposta(comparador1bit_3_nao_tem_resposta));
  comparador1bit comparador1bit_4 (
    .deve_comparar(comparador1bit_3_nao_tem_resposta), .a0(a0), .d0(b0),
    .maior_que(comparador1bit_4_maior_que));  // open: nao_tem_resposta
  or or_1 (maior_que, comparador1bit_1_maior_que, comparador1bit_2_maior_que, comparador1bit_3_maior_que, comparador1bit_4_maior_que);
endmodule
