// Logisim project somador_e_subtratores.circ as structural Verilog: 10 circuits, main circuit main
module main (
);

  soma4bits soma4bits_1 ();  // open: A3, A2, A1, A0, B3, B2, B1, B0, S_0, S_1, S_2, S_3, S_overflow
endmodule

module soma1bit (
  input  Carry_ant,
  input  A,
  input  B,
  output Soma,
  output Carry
);

  wire meio_somador_1_s_soma, meio_somador_1_t_soma, meio_somador_2_t_soma;

  meio_somador meio_somador_1 (.A(A), .B(Carry_ant), .S_soma(meio_somador_1_s_soma), .T_soma(meio_somador_1_t_soma));
  meio_somador meio_somador_2 (.A(meio_somador_1_s_soma), .B(B), .S_soma(Soma), .T_soma(meio_somador_2_t_soma));
  or or_1 (Carry, meio_somador_1_t_soma, meio_somador_2_t_soma);
endmodule

module soma4bits (
  input  A3,
  input  A2,
  input  A1,
  input  A0,
  input  B3,
  input  B2,
  input  B1,
  input  B0,
  output S_0,
  output S_1,
  output S_2,
  output S_3,
  output S_overflow
);

  wire soma1bit_1_carry, soma1bit_2_carry, soma1bit_3_carry;

  soma1bit soma1bit_1 (.Carry_ant(1'b0), .A(A0), .B(B0), .Soma(S_0), .Carry(soma1bit_1_carry));
  soma1bit soma1bit_2 (.Carry_ant(soma1bit_1_carry), .A(A1), .B(B1), .Soma(S_1), .Carry(soma1bit_2_carry));
  soma1bit soma1bit_3 (.Carry_ant(soma1bit_2_carry), .A(A2), .B(B2), .Soma(S_2), .Carry(soma1bit_3_carry));
  soma1bit soma1bit_4 (.Carry_ant(soma1bit_3_carry), .A(A3), .B(B3), .Soma(S_3), .Carry(S_overflow));
endmodule

module meio_somador (
  input  A,
  input  B,
  output S_soma,
  output T_soma
);

  wire and_1_out, and_2_out, not_1_out, not_2_out;

  not not_1 (not_1_out, A);
  not not_2 (not_2_out, B);
  and and_1 (and_1_out, not_1_out, B);
  and and_2 (and_2_out, A, not_2_out);
  and and_3 (T_soma, A, B);
  or or_1 (S_soma, and_1_out, and_2_out);
endmodule

module meio_subtrator (
  input  A,
  input  B,
  output S_sub,
  output Carry
);

  wire and_1_out, and_2_out, not_1_out, not_2_out;

  not not_1 (not_1_out, A);
  not not_2 (not_2_out, B);
  and and_1 (and_1_out, not_1_out, B);
  and and_2 (and_2_out, A, not_2_out);
  and and_3 (Carry, not_1_out, B);
  or or_1 (S_sub, and_1_out, and_2_out);
endmodule

module sub1bit (
  input  Carry_ant,
  input  A,
  input  B,
  output Sub,
  output Carry
);

  wire meio_subtrator_1_carry, meio_subtrator_1_s_sub, meio_subtrator_2_carry;

  meio_subtrator meio_subtrator_1 (
    .A(A), .B(Carry_ant), .S_sub(meio_subtrator_1_s_sub), .Carry(meio_subtrator_1_carry));
  meio_subtrator meio_subtrator_2 (.A(meio_subtrator_1_s_sub), .B(B), .S_sub(Sub), .Carry(meio_subtrator_2_carry));
  or or_1 (Carry, meio_subtrator_1_carry, meio_subtrator_2_carry);
endmodule

module sub4bits (
  input  A3,
  input  A2,
  input  A1,
  input  A0,
  input  B3,
  input  B2,
  input  B1,
  input  B0,
  output S_0,
  output S_1,
  output S_2,
  output S_3,
  output S_overflow
);

  wire sub1bit_1_carry, sub1bit_2_carry, sub1bit_3_carry;

  sub1bit sub1bit_1 (.Carry_ant(1'b0), .A(A0), .B(B0), .Sub(S_0), .Carry(sub1bit_1_carry));
  sub1bit sub1bit_2 (.Carry_ant(sub1bit_1_carry), .A(A1), .B(B1), .Sub(S_1), .Carry(sub1bit_2_carry));
  sub1bit sub1bit_3 (.Carry_ant(sub1bit_2_carry), .A(A2), .B(B2), .Sub(S_2), .Carry(sub1bit_3_carry));
  sub1bit sub1bit_4 (.Carry_ant(sub1bit_3_carry), .A(A3), .B(B3), .Sub(S_3), .Carry(S_overflow));
endmodule

module sub_complemento_de_2 (
  input  A3,
  input  A2,
  input  A1,
  input  A0,
  input  B0,
  input  B1,
  input  B2,
  input  B3,
  output S_0,
  output S_1,
  output S_2,
  output S_3
);

  wire complemento2_1_s_0, complemento2_1_s_1, complemento2_1_s_2, complemento2_1_s_3;

  complemento2 complemento2_1 (
    .B0(B0), .B1(B1), .B2(B2), .B3(B3), .S_0(complemento2_1_s_0), .S_1(complemento2_1_s_1),
    .S_2(complemento2_1_s_2), .S_3(complemento2_1_s_3));
  soma4bits soma4bits_1 (
    .A3(A3), .A2(A2), .A1(A1), .A0(A0), .B3(complemento2_1_s_3), .B2(complemento2_1_s_2),
    .B1(complemento2_1_s_1), .B0(complemento2_1_s_0), .S_0(S_0), .S_1(S_1), .S_2(S_2), .S_3(S_3));  // open: S_overflow
endmodule

module complemento2 (
  input  B0,
  input  B1,
  input  B2,
  input  B3,
  output S_0,
  output S_1,
  output S_2,
  output S_3
);

  wire complemento1_1_i_b0, complemento1_1_i_b1, complemento1_1_i_b2, complemento1_1_i_b3;

  complemento1 complemento1_1 (
    .B0(B0), .B1(B1), .B2(B2), .B3(B3), .I_B0(complemento1_1_i_b0), .I_B1(complemento1_1_i_b1),
    .I_B2(complemento1_1_i_b2), .I_B3(complemento1_1_i_b3));
  soma4bits soma4bits_1 (
    .A3(1'b0), .A2(1'b0), .A1(1'b0), .A0(1'b1), .B3(complemento1_1_i_b3), .B2(complemento1_1_i_b2),
    .B1(complemento1_1_i_b1), .B0(complemento1_1_i_b0), .S_0(S_0), .S_1(S_1), .S_2(S_2), .S_3(S_3));  // open: S_overflow
endmodule

module complemento1 (
  input  B0,
  input  B1,
  input  B2,
  input  B3,
  output I_B0,
  output I_B1,
  output I_B2,
  output I_B3
);

  not not_1 (I_B0, B0);
  not not_2 (I_B1, B1);
  not not_3 (I_B2, B2);
  not not_4 (I_B3, B3);
endmodule
