// Logisim project trabalho01_circuitos-portasLogicas.circ as structural Verilog: 5 circuits, main circuit Dec2Bin_4bits
module Dec2Bin_4bits (
  input  A0,
  input  A1,
  input  A2,
  input  A3,
  input  A4,
  input  A5,
  input  A6,
  input  A7,
  input  A8,
  input  A9,
  output b0,
  output b1,
  output b2,
  output b3
);

  or or_1 (b3, A9, A8);
  or or_2 (b2, A4, A5, A6, A7);
  or or_3 (b1, A2, A3, A6, A7);
  or or_4 (b0, A7, A1, A3, A5, A9);
endmodule

module Bin2Dec_7Seg_5bits (
  input  [4:0] binario,
  output d1,
  output d2,
  output d3,
  output d4,
  output d5,
  output d6,
  output d7,
  output u1,
  output u2,
  output u3,
  output u4,
  output u5,
  output u6,
  output u7
);

  wire bloco_desena_1_w, bloco_desena_1_x, bloco_desena_1_y, bloco_desena_1_z, bloco_unidade_1_w,
       bloco_unidade_1_x, bloco_unidade_1_y, bloco_unidade_1_z;

  bloco_desena bloco_desena_1 (
    .a(binario[4]), .b(binario[3]), .c(binario[2]), .d(binario[1]), .e(binario[0]), .w(bloco_desena_1_w),
    .x(bloco_desena_1_x), .y(bloco_desena_1_y), .z(bloco_desena_1_z));
  bloco_unidade bloco_unidade_1 (
    .a(binario[4]), .b(binario[3]), .c(binario[2]), .d(binario[1]), .e(binario[0]), .w(bloco_unidade_1_w),
    .x(bloco_unidade_1_x), .y(bloco_unidade_1_y), .z(bloco_unidade_1_z));
  codificador7seguimeto codificador7seguimeto_1 (
    .a(bloco_desena_1_w), .b(bloco_desena_1_x), .c(bloco_desena_1_y), .d(bloco_desena_1_z), .s1(d1), .s2(d2),
    .s3(d3), .s4(d4), .s5(d5), .s6(d6), .s7(d7));
  codificador7seguimeto codificador7seguimeto_2 (
    .a(bloco_unidade_1_w), .b(bloco_unidade_1_x), .c(bloco_unidade_1_y), .d(bloco_unidade_1_z), .s1(u1),
    .s2(u2), .s3(u3), .s4(u4), .s5(u5), .s6(u6), .s7(u7));
endmodule

module codificador7seguimeto (
  input  a,
  input  b,
  input  c,
  input  d,
  output s1,
  output s2,
  output s3,
  output s4,
  output s5,
  output s6,
  output s7
);

  wire and_1_out, and_2_out, and_3_out, and_4_out, and_5_out, and_6_out, and_7_out, and_8_out, and_9_out,
       and_10_out, and_11_out, and_12_out, and_13_out, and_14_out, and_15_out, and_16_out, and_17_out,
       and_18_out, and_19_out, and_20_out, and_21_out, and_22_out, and_23_out, and_24_out, and_25_out,
       and_26_out, and_27_out, not_1_out, not_2_out, not_3_out, not_4_out;

  not not_1 (not_1_out, a);
  not not_2 (not_2_out, b);
  not not_3 (not_3_out, c);
  not not_4 (not_4_out, d);
  and and_1 (and_1_out, not_2_out, not_4_out);
  and and_2 (and_2_out, b, d);
  and and_3 (and_3_out, not_1_out, not_2_out);
  and and_4 (and_4_out, not_3_out, not_4_out);
  and and_5 (and_5_out, not_1_out, c, d);
  and and_6 (and_6_out, not_2_out, d);
  and and_7 (and_7_out, a, not_3_out);
  and and_8 (and_8_out, a, b, not_4_out);
  and and_9 (and_9_out, not_1_out, d);
  and and_10 (and_10_out, not_3_out, d);
  and and_11 (and_11_out, not_1_out, b);
  and and_12 (and_12_out, not_2_out, not_3_out);
  and and_13 (and_13_out, a, c, not_4_out);
  and and_14 (and_14_out, not_2_out, not_4_out);
  and and_15 (and_15_out, not_1_out, not_2_out, c);
  and and_16 (and_16_out, not_1_out, b, not_3_out, d);
  and and_17 (and_17_out, c, not_4_out);
  and and_18 (and_18_out, a, not_2_out, not_3_out);
  and and_19 (and_19_out, a, not_4_out);
  and and_20 (and_20_out, not_2_out, not_4_out);
  and and_21 (and_21_out, c, not_4_out);
  and and_22 (and_22_out, not_3_out, not_4_out);
  and and_23 (and_23_out, b, not_3_out);
  and and_24 (and_24_out, b, not_4_out);
  and and_25 (and_25_out, not_2_out, c);
  and and_26 (and_26_out, b, not_3_out);
  and and_27 (and_27_out, c, not_4_out);
  or or_1 (s1, and_1_out, c, and_2_out, a);
  or or_2 (s2, and_3_out, and_4_out, and_5_out, and_6_out, and_7_out, and_8_out);
  or or_3 (s3, and_9_out, and_10_out, and_11_out, and_12_out, and_13_out);
  or or_4 (s4, and_14_out, and_15_out, and_16_out, and_17_out, and_18_out, and_19_out);
  or or_5 (s5, and_20_out, and_21_out);
  or or_6 (s6, and_22_out, and_23_out, and_24_out, a);
  or or_7 (s7, and_25_out, and_26_out, a, and_27_out);
endmodule

module bloco_desena (
  input  a,
  input  b,
  input  c,
  input  d,
  input  e,
  output w,
  output x,
  output y,
  output z
);

  wire and_1_out, and_2_out, and_3_out, and_4_out, and_5_out, and_6_out, not_1_out, not_2_out, not_3_out;

  not not_1 (not_1_out, a);
  not not_2 (not_2_out, b);
  not not_3 (not_3_out, c);
  and and_1 (and_1_out, a, c);
  and and_2 (and_2_out, a, b);
  and and_3 (and_3_out, a, not_2_out, not_3_out);
  and and_4 (and_4_out, not_1_out, b, d);
  and and_5 (and_5_out, not_1_out, b, c);
  and and_6 (and_6_out, b, c, d);
  or or_1 (y, and_1_out, and_2_out);
  or or_2 (z, and_3_out, and_4_out, and_5_out, and_6_out);

  assign w = 1'b0;
  assign x = 1'b0;
endmodule

module bloco_unidade (
  input  a,
  input  b,
  input  c,
  input  d,
  input  e,
  output w,
  output x,
  output y,
  output z
);

  wire and_1_out, and_2_out, and_3_out, and_4_out, and_5_out, and_6_out, and_7_out, and_8_out, and_9_out,
       and_10_out, and_11_out, and_12_out, not_1_out, not_2_out, not_3_out, not_4_out;

  not not_1 (not_1_out, a);
  not not_2 (not_2_out, b);
  not not_3 (not_3_out, c);
  not not_4 (not_4_out, d);
  and and_1 (and_1_out, a, not_2_out, not_3_out, d);
  and and_2 (and_2_out, not_1_out, b, not_3_out, not_4_out);
  and and_3 (and_3_out, a, b, c, not_4_out);
  and and_4 (and_4_out, a, not_3_out, not_4_out);
  and and_5 (and_5_out, not_1_out, not_2_out, c);
  and and_6 (and_6_out, a, b, not_3_out);
  and and_7 (and_7_out, not_1_out, c, d);
  and and_8 (and_8_out, a, not_2_out, not_3_out, not_4_out);
  and and_9 (and_9_out, not_1_out, not_2_out, d);
  and and_10 (and_10_out, not_2_out, c, d);
  and and_11 (and_11_out, a, b, not_3_out, d);
  and and_12 (and_12_out, not_1_out, b, c, not_4_out);
  or or_1 (w, and_1_out, and_2_out, and_3_out);
  or or_2 (x, and_4_out, and_5_out, and_6_out, and_7_out);
  or or_3 (y, and_8_out, and_9_out, and_10_out, and_11_out, and_12_out);

  assign z = e;
endmodule
