// Logisim project trabalho1.circ as structural Verilog
module main (
  input  in_1,
  input  in_2,
  input  in_3,
  input  in_4,
  input  in_5,
  input  in_6,
  input  in_7,
  input  in_8,
  input  in_9,
  input  in_10,
  input  in_11,
  input  in_12,
  input  in_13,
  input  in_14,
  input  in_15,
  input  in_16,
  input  in_17,
  input  in_18,
  output out_19,
  output out_20,
  output out_21,
  output out_22,
  output out_23,
  output out_24,
  output out_25,
  output out_26,
  output out_27,
  output out_28,
  output out_29,
  output out_30,
  output out_31
);

  wire a0, a1, b0, b1, c0, c1, d0, d1, e0, e1, f0, f1, g0, g1;

  meu_bin2dec5bits meu_bin2dec5bits_1 (
    .BIN_4(in_14), .BIN_3(in_15), .BIN_2(in_16), .BIN_1(in_17), .BIN_0(in_18), .S_a0(a0), .S_b0(b0),
    .S_c0(c0), .S_d0(d0), .S_e0(e0), .S_f0(f0), .S_g0(g0), .S_a1(a1), .S_b1(b1), .S_c1(c1), .S_d1(d1),
    .S_e1(e1), .S_f1(f1), .S_g1(g1));
  _7_Segment_Display u_7_segment_display_1 (.g(g1), .f(f1), .a(a1), .b(b1), .e(e1), .d(d1), .c(c1));  // open: dp
  _7_Segment_Display u_7_segment_display_2 (.g(g0), .f(f0), .a(a0), .b(b0), .e(e0), .d(d0), .c(c0));  // open: dp
endmodule

module binario_pra_decimal_5bits (
  input  [4:0] binario
);

  wire a0, a1, b0, b1, bin2dec_7seg_5bits_1_d1, bin2dec_7seg_5bits_1_d2, bin2dec_7seg_5bits_1_d3,
       bin2dec_7seg_5bits_1_d4, bin2dec_7seg_5bits_1_d5, bin2dec_7seg_5bits_1_d6, bin2dec_7seg_5bits_1_d7,
       bin2dec_7seg_5bits_1_u1, bin2dec_7seg_5bits_1_u2, bin2dec_7seg_5bits_1_u3, bin2dec_7seg_5bits_1_u4,
       bin2dec_7seg_5bits_1_u5, bin2dec_7seg_5bits_1_u6, bin2dec_7seg_5bits_1_u7, c0, c1, d0, d1, e0, e1, f0,
       f1, g0, g1;
  wire [4:0] undriven;

  Bin2Dec_7Seg_5bits bin2dec_7seg_5bits_1 (
    .binario(undriven), .d1(bin2dec_7seg_5bits_1_d1), .d2(bin2dec_7seg_5bits_1_d2),
    .d3(bin2dec_7seg_5bits_1_d3), .d4(bin2dec_7seg_5bits_1_d4), .d5(bin2dec_7seg_5bits_1_d5),
    .d6(bin2dec_7seg_5bits_1_d6), .d7(bin2dec_7seg_5bits_1_d7), .u1(bin2dec_7seg_5bits_1_u1),
    .u2(bin2dec_7seg_5bits_1_u2), .u3(bin2dec_7seg_5bits_1_u3), .u4(bin2dec_7seg_5bits_1_u4),
    .u5(bin2dec_7seg_5bits_1_u5), .u6(bin2dec_7seg_5bits_1_u6), .u7(bin2dec_7seg_5bits_1_u7));
  // meu_bin2dec5bits meu_bin2dec5bits_1: pin names not known; wires that end beside it: binario, a0, b0, c0, d0, e0, f0, g0, a1, b1, c1, d1, e1, f1, g1
  _7_Segment_Display desena (
    .g(bin2dec_7seg_5bits_1_d7), .f(bin2dec_7seg_5bits_1_d6), .a(bin2dec_7seg_5bits_1_d1),
    .b(bin2dec_7seg_5bits_1_d2), .e(bin2dec_7seg_5bits_1_d5), .d(bin2dec_7seg_5bits_1_d4),
    .c(bin2dec_7seg_5bits_1_d3));  // open: dp
  _7_Segment_Display unidade (
    .g(bin2dec_7seg_5bits_1_u7), .f(bin2dec_7seg_5bits_1_u6), .a(bin2dec_7seg_5bits_1_u1),
    .b(bin2dec_7seg_5bits_1_u2), .e(bin2dec_7seg_5bits_1_u5), .d(bin2dec_7seg_5bits_1_u4),
    .c(bin2dec_7seg_5bits_1_u3));  // open: dp
  _7_Segment_Display u_7_segment_display_1 (.g(g1), .f(f1), .a(a1), .b(b1), .e(e1), .d(d1), .c(c1));  // open: dp
  _7_Segment_Display u_7_segment_display_2 (.g(g0), .f(f0), .a(a0), .b(b0), .e(e0), .d(d0), .c(c0));  // open: dp

  // Notes on the sheet:
  //   Bin2Dec_7Seg_5bits
endmodule

module decimal_pra_binario_5bits (
  input  a0,
  input  a1,
  input  a2,
  input  a3,
  input  a4,
  input  a5,
  input  a6,
  input  a7,
  input  a8,
  input  a9,
  output A,
  output B,
  output C,
  output D,
  output [3:0] out_15
);

  meu_dec2bin4bits meu_dec2bin4bits_1 (
    .a0(a0), .a1(a1), .a2(a2), .a3(a3), .a4(a4), .a5(a5), .a6(a6), .a7(a7), .a8(a8), .a9(a9), .A(A), .B(B),
    .C(C), .D(D));
  Dec2Bin_4bits dec2bin_4bits_1 (
    .A0(a0), .A1(a1), .A2(a2), .A3(a3), .A4(a4), .A5(a5), .A6(a6), .A7(a7), .A8(a8), .A9(a9), .b0(out_15[0]),
    .b1(out_15[1]), .b2(out_15[2]), .b3(out_15[3]));

  // Notes on the sheet:
  //   Dec2Bin_4bits
endmodule

// VHDL entity meu_bin2bcd5bits, as the project stores it:
LIBRARY ieee;
USE ieee.std_logic_1164.all;

ENTITY meu_bin2bcd5bits IS
  PORT (
  	A, B, C, D, E: IN std_logic;
  	BCDu_3, BCDu_2, BCDu_1, BCDu_0: OUT std_logic;
  	BCDd_3, BCDd_2, BCDd_1, BCDd_0: OUT std_logic
    );
END meu_bin2bcd5bits;

ARCHITECTURE TypeArchitecture OF meu_bin2bcd5bits IS
    
BEGIN
	shift_bcd: process(BIN) is
		variable BIN_org: std_logic_vector(4 DOWNTO 0);
    		variable BCD0_org, BCD1_org: std_logic_vector(3 DOWNTO 0);
    		variable BIN_shf: std_logic_vector(4 DOWNTO 0);
    		variable BCD0_shf, BCD1_shf: std_logic_vector(3 DOWNTO 0);
	begin
		BIN_org := BIN;
		BCD0_org := "0000";
		BCD1_org := "0000";
		for i in 4 downto 0 loop
		   	--somar 3 quando maior que 5
			case BCD0_org is
				when "0101" =>
					BCD0_shf := "1000";
				when "0110" =>
					BCD0_shf := "1001";
				when "0111" =>
					BCD0_shf := "1010";
				when "1000" =>
					BCD0_shf := "1011";
				when "1001" =>
					BCD0_shf := "1100";
				when "1010" =>
					BCD0_shf := "1101";
				when "1011" =>
					BCD0_shf := "1110";
				when "1100" =>
					BCD0_shf := "1111";
				when others =>
					BCD0_shf := BCD0_org;
		    	end case;
				
			case BCD1_org is
				when "0101" =>
					BCD1_shf := "1000";
				when "0110" =>
					BCD1_shf := "1001";
				when "0111" =>
					BCD1_shf := "1010";
				when "1000" =>
					BCD1_shf := "1011";
				when "1001" =>
					BCD1_shf := "1100";
				when "1010" =>
					BCD1_shf := "1101";
				when "1011" =>
					BCD1_shf := "1110";
				when "1100" =>
					BCD1_shf := "1111";
				when others =>
					BCD1_shf := BCD1_org;
			end case;
			BCD0_org := BCD0_shf;
			BCD1_org := BCD1_shf;
			
			--mudar primeira celula do bcd
			for i in 2 downto 0 loop
				BCD1_shf(i + 1) := BCD1_org(i);
			end loop;
			BCD1_shf(0) := BCD0_org(3);
	
			--mudar segunda celula do bcd
			for i in 2 downto 0 loop
				BCD0_shf(i + 1) := BCD0_org(i);
			end loop;
			BCD0_shf(0) := BIN_org(4);
	
			--mudar o binario
			for i in 3 downto 0 loop
				BIN_shf(i + 1) := BIN_org(i);
			end loop;
			BIN_shf(0) := '0';
	
			BIN_org := BIN_shf;
			BCD0_org := BCD0_shf;
			BCD1_org := BCD1_shf;

		 end loop;
		 BCD0 <= BCD0_org;
		 BCD1 <= BCD1_org;
	end process shift_bcd;

END TypeArchitecture;

// VHDL entity meu_dec2bin4bits, as the project stores it:
LIBRARY ieee;
USE ieee.std_logic_1164.all;

ENTITY meu_dec2bin4bits IS
  PORT (
    a0, a1, a2, a3, a4, a5, a6, a7, a8, a9: IN std_logic;
    A, B, C, D: OUT std_logic
    );
END meu_dec2bin4bits;

ARCHITECTURE TypeArchitecture OF meu_dec2bin4bits IS

BEGIN
	A <= a9 or a8;
	B <= a4 or a5 or a6 or a7;
	C <= a2 or a3 or a6 or a7;
	D <= a1 or a3 or a5 or a7 or a9;

END TypeArchitecture;

// VHDL entity meu_bin2dec5bits, as the project stores it:
LIBRARY ieee;
USE ieee.std_logic_1164.all;

ENTITY meu_bin2dec5bits IS
  PORT (
  	--entrada do binario de 5 bits
  	BIN_4, BIN_3, BIN_2, BIN_1, BIN_0: IN std_logic;

  	--saídas dos displays
  	S_a0, S_b0, S_c0, S_d0, S_e0, S_f0, S_g0: OUT std_logic; --display da unidade
  	S_a1, S_b1, S_c1, S_d1, S_e1, S_f1, S_g1: OUT std_logic  --display da dezena
    );
END meu_bin2dec5bits;

ARCHITECTURE TypeArchitecture OF meu_bin2dec5bits IS
    signal a1, b1, c1, d1: std_logic; --auxiliares
    signal e1, f1, g1, h1: std_logic; --auxiliares 
BEGIN
	process(BIN_4, BIN_3, BIN_2, BIN_1, BIN_0) is
		variable BIN_org: std_logic_vector(4 DOWNTO 0);
    		variable BCD0_org, BCD1_org: std_logic_vector(3 DOWNTO 0);
    		
    		variable BIN_shf: std_logic_vector(4 DOWNTO 0);
    		variable BCD0_shf, BCD1_shf: std_logic_vector(3 DOWNTO 0);
    		
    		variable a, b, c, d: std_logic;
    		variable e, f, g, h: std_logic;
	begin
		BIN_org(4) := BIN_4; BIN_org(3) := BIN_3;
		BIN_org(2) := BIN_2; BIN_org(1) := BIN_1;
		BIN_org(0) := BIN_0;
		
		BCD0_org := "0000";
		BCD1_org := "0000";
		for i in 4 downto 0 loop
			a := BCD0_org(3); b := BCD0_org(2);
			c := BCD0_org(1); d := BCD0_org(0);
			
			e := BCD1_org(3); f := BCD1_org(2);
			g := BCD1_org(1); h := BCD1_org(0);
			
		   	--somar 3 quando maior que 5
		   	BCD0_shf(3) := ((b and d) or (b and c)) or a;
		   	BCD0_shf(2) := (b and not c and not d) or (a and d) or (a and c);
		   	BCD0_shf(1) := (not a and not b and c) or (c and d) or (a and not c and not d) or (a and b and not d);
		   	BCD0_shf(0) := (not a and not b and d) or (not a and b and c and not d) or (a and not b and not d) or (a and b and d) or (a and not c and not d);
				
			BCD1_shf(3) := (f and h) or (f and g) or e;
		   	BCD1_shf(2) := (f and not g and not h) or (e and h) or (e and g);
		   	BCD1_shf(1) := (not e and not f and g) or (g and h) or (e and not g and not h) or (e and f and not h);
		   	BCD1_shf(0) := (not e and not f and h) or (not e and f and g and not h) or (e and not f and not h) or (e and f and h) or (e and not g and not h);
			
			BCD0_org := BCD0_shf;
			BCD1_org := BCD1_shf;
			
			--mudar primeira celula do bcd
			BCD1_shf(3) := BCD1_org(2);
			BCD1_shf(2) := BCD1_org(1);
			BCD1_shf(1) := BCD1_org(0);
			BCD1_shf(0) := BCD0_org(3);
			
			--mudar segunda celula do bcd
			BCD0_shf(3) := BCD0_org(2);
			BCD0_shf(2) := BCD0_org(1);
			BCD0_shf(1) := BCD0_org(0);
			BCD0_shf(0) := BIN_org(4);
			
			--mudar o binario
			BIN_shf(4) := BIN_org(3);
			BIN_shf(3) := BIN_org(2);
			BIN_shf(2) := BIN_org(1);
			BIN_shf(1) := BIN_org(0);
			BIN_shf(0) := '0';
			
			BIN_org := BIN_shf;
			BCD0_org := BCD0_shf;
			BCD1_org := BCD1_shf;
		 end loop;
		 
		--Bits do bcd da unidade
		a1 <= BCD0_org(3); b1 <= BCD0_org(2);
		c1 <= BCD0_org(1); d1 <= BCD0_org(0);
		
		--Bits do bcd da dezena
		e1 <= BCD1_org(3); f1 <= BCD1_org(2);
		g1 <= BCD1_org(1); h1 <= BCD1_org(0);
	end process;
	
	--Primeiro display
	S_a0 <= a1 or c1 or not ((not b1 and d1) or (b1 and not d1));
	
	S_b0 <= not b1 or not ((not c1 and d1) or (c1 and not d1));
	
	S_c0 <= b1 or not c1 or d1;
	
	S_d0 <= a1 or 
		(not b1 and not d1) or
		(not b1 and c1) or
		(c1 and not d1) or
		(b1 and not c1 and d1);

	S_e0 <= (not b1 and not d1) or
		(c1 and not d1);

	S_f0 <= a1 or
		(not c1 and not d1) or
		(b1 and not c1) or
		(b1 and not d1);

	S_g0 <= a1 or
		((not b1 and c1) or (b1 and not c1)) or
		(c1 and not d1);

	--Segundo display
	S_a1 <= e1 or g1 or not ((not f1 and h1) or (f1 and not h1));
	
	S_b1 <= not f1 or not ((not g1 and h1) or (g1 and not h1));
	
	S_c1 <= f1 or not g1 or h1;
	
	S_d1 <= e1 or 
		(not f1 and not h1) or
		(not f1 and g1) or
		(g1 and not h1) or
		(f1 and not g1 and h1);

	S_e1 <= (not f1 and not h1) or
		(g1 and not h1);

	S_f1 <= e1 or
		(not g1 and not h1) or
		(f1 and not g1) or
		(f1 and not h1);

	S_g1 <= e1 or
		((not g1 and f1) or (g1 and not f1)) or
		(g1 and not h1);
	
END TypeArchitecture;

// VHDL entity meu_bcd2dec, as the project stores it:
LIBRARY ieee;
USE ieee.std_logic_1164.all;

ENTITY meu_bcd2dec IS
  PORT (
  	A, B, C, D: IN std_logic;
  	a, b, c, d, e, f, g, h: OUT std_logic
    );
END meu_bcd2dec;

ARCHITECTURE TypeArchitecture OF meu_bcd2dec IS
    
BEGIN
	--Primeiro display
	a <= A or C or not (B xor D);
	
	b <= not B or not (C xor D);
	
	c <= B or not C or D;
	
	d <= A or 
		(not B and not D) or
		(not B and C) or
		(C and not D) or
		(B and not C and D);

	e <= (not B and not D) or
		(C and not D);

	f <= A or
		(not C and not D) or
		(B and not C) or
		(B and not D);

	g <= A or
		(B xor C) or
		(C and not D);
	
END TypeArchitecture;
