// Logisim project trabalho1_completo.circ as structural Verilog
module main (
  input  [4:0] in_1,
  output [3:0] out_2,
  output [3:0] out_3
);

  wire a0, a00, A1, a1_t, a2, a3, a4, a5, a6, a7, a8, a9, b00, B1, c0, C1, d0, D1, d1_t, d2, d3, d4, d5, d6,
       d7, e0, E1, f0, F1, g0, G1, u1, u2, u3, u4, u5, u6, u7;

  Button u_A0 (.out(a0));
  Button u_A1 (.out(a1_t));
  Button u_A2 (.out(a2));
  Button u_A3 (.out(a3));
  Button u_A4 (.out(a4));
  Button u_A5 (.out(a5));
  Button u_A6 (.out(a6));
  Button u_A7 (.out(a7));
  Button u_A8 (.out(a8));
  Button u_A9 (.out(a9));
  Dec2Bin_4bits dec2bin_4bits_1 (
    .A0(a0), .A1(a1_t), .A2(a2), .A3(a3), .A4(a4), .A5(a5), .A6(a6), .A7(a7), .A8(a8), .A9(a9),
    .b0(out_2[0]), .b1(out_2[1]), .b2(out_2[2]), .b3(out_2[3]));
  Bin2Dec_7Seg_5bits bin2dec_7seg_5bits_1 (
    .b4(in_1[4]), .b3(in_1[3]), .b2(in_1[2]), .b1(in_1[1]), .b0(in_1[0]), .d1(d1_t), .d2(d2), .d3(d3),
    .d4(d4), .d5(d5), .d6(d6), .d7(d7), .u1(u1), .u2(u2), .u3(u3), .u4(u4), .u5(u5), .u6(u6), .u7(u7));
  _7_Segment_Display u_7_segment_display_1 (.g(d7), .f(d6), .a(d1_t), .b(d2), .e(d5), .d(d4), .c(d3));  // open: dp
  _7_Segment_Display u_7_segment_display_2 (.g(u7), .f(u6), .a(u1), .b(u2), .e(u5), .d(u4), .c(u3));  // open: dp
  meu_dec2bin4bits meu_dec2bin4bits_1 (
    .a0(a0), .a1(a1_t), .a2(a2), .a3(a3), .a4(a4), .a5(a5), .a6(a6), .a7(a7), .a8(a8), .a9(a9), .A(out_3[0]),
    .B(out_3[1]), .C(out_3[2]), .D(out_3[3]));
  meu_bin2dec5bits meu_bin2dec5bits_1 (
    .BIN_4(in_1[4]), .BIN_3(in_1[3]), .BIN_2(in_1[2]), .BIN_1(in_1[1]), .BIN_0(in_1[0]), .S_a0(a00),
    .S_b0(b00), .S_c0(c0), .S_d0(d0), .S_e0(e0), .S_f0(f0), .S_g0(g0), .S_a1(A1), .S_b1(B1), .S_c1(C1),
    .S_d1(D1), .S_e1(E1), .S_f1(F1), .S_g1(G1));
  _7_Segment_Display u_7_segment_display_3 (.g(G1), .f(F1), .a(A1), .b(B1), .e(E1), .d(D1), .c(C1));  // open: dp
  _7_Segment_Display u_7_segment_display_4 (.g(g0), .f(f0), .a(a00), .b(b00), .e(e0), .d(d0), .c(c0));  // open: dp

  // Other names for the same wires on the sheet: b0 = in_1[0]; b1_t = in_1[1]; b2 = in_1[2]; b3 = in_1[3];
  //   b4 = in_1[4]

  // Notes on the sheet:
  //   PORTAS LOGICAS
  //   VHDL
endmodule

module Dec2Bin_4bits (
  input  A0,
  input  A1,
  input  A2,
  input  A3,
  input  A4,
  input  A5,
  input  A6,
  input  A7,
  input  A8,
  input  A9,
  output b0,
  output b1,
  output b2,
  output b3
);

  or or_1 (b3, A9, A8);
  or or_2 (b2, A4, A5, A6, A7);
  or or_3 (b1, A2, A3, A6, A7);
  or or_4 (b0, A7, A1, A3, A5, A9);
endmodule

module Bin2Dec_7Seg_5bits (
  input  b4,
  input  b3,
  input  b2,
  input  b1,
  input  b0,
  output d1,
  output d2,
  output d3,
  output d4,
  output d5,
  output d6,
  output d7,
  output u1,
  output u2,
  output u3,
  output u4,
  output u5,
  output u6,
  output u7
);

  wire bloco_desena_1_w, bloco_desena_1_x, bloco_desena_1_y, bloco_desena_1_z, bloco_unidade_1_w,
       bloco_unidade_1_x, bloco_unidade_1_y, bloco_unidade_1_z;

  bloco_desena bloco_desena_1 (
    .a(b4), .b(b3), .c(b2), .d(b1), .e(b0), .w(bloco_desena_1_w), .x(bloco_desena_1_x), .y(bloco_desena_1_y),
    .z(bloco_desena_1_z));
  bloco_unidade bloco_unidade_1 (
    .a(b4), .b(b3), .c(b2), .d(b1), .e(b0), .w(bloco_unidade_1_w), .x(bloco_unidade_1_x),
    .y(bloco_unidade_1_y), .z(bloco_unidade_1_z));
  codificador7seguimeto codificador7seguimeto_1 (
    .a(bloco_desena_1_w), .b(bloco_desena_1_x), .c(bloco_desena_1_y), .d(bloco_desena_1_z), .s1(d1), .s2(d2),
    .s3(d3), .s4(d4), .s5(d5), .s6(d6), .s7(d7));
  codificador7seguimeto codificador7seguimeto_2 (
    .a(bloco_unidade_1_w), .b(bloco_unidade_1_x), .c(bloco_unidade_1_y), .d(bloco_unidade_1_z), .s1(u1),
    .s2(u2), .s3(u3), .s4(u4), .s5(u5), .s6(u6), .s7(u7));
endmodule

module codificador7seguimeto (
  input  a,
  input  b,
  input  c,
  input  d,
  output s1,
  output s2,
  output s3,
  output s4,
  output s5,
  output s6,
  output s7
);

  wire and_1_out, and_2_out, and_3_out, and_4_out, and_5_out, and_6_out, and_7_out, and_8_out, and_9_out,
       and_10_out, and_11_out, and_12_out, and_13_out, and_14_out, and_15_out, and_16_out, and_17_out,
       and_18_out, and_19_out, and_20_out, and_21_out, and_22_out, and_23_out, and_24_out, and_25_out,
       and_26_out, and_27_out, not_1_out, not_2_out, not_3_out, not_4_out;

  not not_1 (not_1_out, a);
  not not_2 (not_2_out, b);
  not not_3 (not_3_out, c);
  not not_4 (not_4_out, d);
  and and_1 (and_1_out, not_2_out, not_4_out);
  and and_2 (and_2_out, b, d);
  and and_3 (and_3_out, not_1_out, not_2_out);
  and and_4 (and_4_out, not_3_out, not_4_out);
  and and_5 (and_5_out, not_1_out, c, d);
  and and_6 (and_6_out, not_2_out, d);
  and and_7 (and_7_out, a, not_3_out);
  and and_8 (and_8_out, a, b, not_4_out);
  and and_9 (and_9_out, not_1_out, d);
  and and_10 (and_10_out, not_3_out, d);
  and and_11 (and_11_out, not_1_out, b);
  and and_12 (and_12_out, not_2_out, not_3_out);
  and and_13 (and_13_out, a, c, not_4_out);
  and and_14 (and_14_out, not_2_out, not_4_out);
  and and_15 (and_15_out, not_1_out, not_2_out, c);
  and and_16 (and_16_out, not_1_out, b, not_3_out, d);
  and and_17 (and_17_out, c, not_4_out);
  and and_18 (and_18_out, a, not_2_out, not_3_out);
  and and_19 (and_19_out, a, not_4_out);
  and and_20 (and_20_out, not_2_out, not_4_out);
  and and_21 (and_21_out, c, not_4_out);
  and and_22 (and_22_out, not_3_out, not_4_out);
  and and_23 (and_23_out, b, not_3_out);
  and and_24 (and_24_out, b, not_4_out);
  and and_25 (and_25_out, not_2_out, c);
  and and_26 (and_26_out, b, not_3_out);
  and and_27 (and_27_out, c, not_4_out);
  or or_1 (s1, and_1_out, c, and_2_out, a);
  or or_2 (s2, and_3_out, and_4_out, and_5_out, and_6_out, and_7_out, and_8_out);
  or or_3 (s3, and_9_out, and_10_out, and_11_out, and_12_out, and_13_out);
  or or_4 (s4, and_14_out, and_15_out, and_16_out, and_17_out, and_18_out, and_19_out);
  or or_5 (s5, and_20_out, and_21_out);
  or or_6 (s6, and_22_out, and_23_out, and_24_out, a);
  or or_7 (s7, and_25_out, and_26_out, a, and_27_out);
endmodule

module bloco_desena (
  input  a,
  input  b,
  input  c,
  input  d,
  input  e,
  output w,
  output x,
  output y,
  output z
);

  wire and_1_out, and_2_out, and_3_out, and_4_out, and_5_out, and_6_out, not_1_out, not_2_out, not_3_out;

  not not_1 (not_1_out, a);
  not not_2 (not_2_out, b);
  not not_3 (not_3_out, c);
  and and_1 (and_1_out, a, c);
  and and_2 (and_2_out, a, b);
  and and_3 (and_3_out, a, not_2_out, not_3_out);
  and and_4 (and_4_out, not_1_out, b, d);
  and and_5 (and_5_out, not_1_out, b, c);
  and and_6 (and_6_out, b, c, d);
  or or_1 (y, and_1_out, and_2_out);
  or or_2 (z, and_3_out, and_4_out, and_5_out, and_6_out);

  assign w = 1'b0;
  assign x = 1'b0;
endmodule

module bloco_unidade (
  input  a,
  input  b,
  input  c,
  input  d,
  input  e,
  output w,
  output x,
  output y,
  output z
);

  wire and_1_out, and_2_out, and_3_out, and_4_out, and_5_out, and_6_out, and_7_out, and_8_out, and_9_out,
       and_10_out, and_11_out, and_12_out, not_1_out, not_2_out, not_3_out, not_4_out;

  not not_1 (not_1_out, a);
  not not_2 (not_2_out, b);
  not not_3 (not_3_out, c);
  not not_4 (not_4_out, d);
  and and_1 (and_1_out, a, not_2_out, not_3_out, d);
  and and_2 (and_2_out, not_1_out, b, not_3_out, not_4_out);
  and and_3 (and_3_out, a, b, c, not_4_out);
  and and_4 (and_4_out, a, not_3_out, not_4_out);
  and and_5 (and_5_out, not_1_out, not_2_out, c);
  and and_6 (and_6_out, a, b, not_3_out);
  and and_7 (and_7_out, not_1_out, c, d);
  and and_8 (and_8_out, a, not_2_out, not_3_out, not_4_out);
  and and_9 (and_9_out, not_1_out, not_2_out, d);
  and and_10 (and_10_out, not_2_out, c, d);
  and and_11 (and_11_out, a, b, not_3_out, d);
  and and_12 (and_12_out, not_1_out, b, c, not_4_out);
  or or_1 (w, and_1_out, and_2_out, and_3_out);
  or or_2 (x, and_4_out, and_5_out, and_6_out, and_7_out);
  or or_3 (y, and_8_out, and_9_out, and_10_out, and_11_out, and_12_out);

  assign z = e;
endmodule

// VHDL entity meu_bin2bcd5bits, as the project stores it:
LIBRARY ieee;
USE ieee.std_logic_1164.all;

ENTITY meu_bin2bcd5bits IS
  PORT (
  	BIN: IN std_logic_vector(4 downto 0);
  	BCD0, BCD1: OUT std_logic_vector(3 downto 0)
    );
END meu_bin2bcd5bits;

ARCHITECTURE TypeArchitecture OF meu_bin2bcd5bits IS
    
BEGIN
	shift_bcd: process(BIN) is
		variable BIN_org: std_logic_vector(4 DOWNTO 0);
    		variable BCD0_org, BCD1_org: std_logic_vector(3 DOWNTO 0);
    		variable BIN_shf: std_logic_vector(4 DOWNTO 0);
    		variable BCD0_shf, BCD1_shf: std_logic_vector(3 DOWNTO 0);
	begin
		BIN_org := BIN;
		BCD0_org := "0000";
		BCD1_org := "0000";
		rayron: for i in 4 downto 0 loop
		   	--somar 3 quando maior que 5
			case BCD0_org is
				when "0101" =>
					BCD0_shf := "1000";
				when "0110" =>
					BCD0_shf := "1001";
				when "0111" =>
					BCD0_shf := "1010";
				when "1000" =>
					BCD0_shf := "1011";
				when "1001" =>
					BCD0_shf := "1100";
				when "1010" =>
					BCD0_shf := "1101";
				when "1011" =>
					BCD0_shf := "1110";
				when "1100" =>
					BCD0_shf := "1111";
				when others =>
					BCD0_shf := BCD0_org;
		    	end case;
				
			case BCD1_org is
				when "0101" =>
					BCD1_shf := "1000";
				when "0110" =>
					BCD1_shf := "1001";
				when "0111" =>
					BCD1_shf := "1010";
				when "1000" =>
					BCD1_shf := "1011";
				when "1001" =>
					BCD1_shf := "1100";
				when "1010" =>
					BCD1_shf := "1101";
				when "1011" =>
					BCD1_shf := "1110";
				when "1100" =>
					BCD1_shf := "1111";
				when others =>
					BCD1_shf := BCD1_org;
			end case;
			BCD0_org := BCD0_shf;
			BCD1_org := BCD1_shf;
			
			--mudar primeira celula do bcd
			for i in 2 downto 0 loop
				BCD1_shf(i + 1) := BCD1_org(i);
			end loop;
			BCD1_shf(0) := BCD0_org(3);
	
			--mudar segunda celula do bcd
			for i in 2 downto 0 loop
				BCD0_shf(i + 1) := BCD0_org(i);
			end loop;
			BCD0_shf(0) := BIN_org(4);
	
			--mudar o binario
			for i in 3 downto 0 loop
				BIN_shf(i + 1) := BIN_org(i);
			end loop;
			BIN_shf(0) := '0';
	
			BIN_org := BIN_shf;
			BCD0_org := BCD0_shf;
			BCD1_org := BCD1_shf;

		 end loop rayron;
		 BCD0 <= BCD0_org;
		 BCD1 <= BCD1_org;
	end process shift_bcd;

END TypeArchitecture;

// VHDL entity meu_dec2bin4bits, as the project stores it:
LIBRARY ieee;
USE ieee.std_logic_1164.all;

ENTITY meu_dec2bin4bits IS
  PORT (
    a0, a1, a2, a3, a4, a5, a6, a7, a8, a9: IN std_logic;
    A, B, C, D: OUT std_logic
    );
END meu_dec2bin4bits;

ARCHITECTURE TypeArchitecture OF meu_dec2bin4bits IS

BEGIN
	A <= a9 or a8;
	B <= a4 or a5 or a6 or a7;
	C <= a2 or a3 or a6 or a7;
	D <= a1 or a3 or a5 or a7 or a9;

END TypeArchitecture;

// VHDL entity meu_bin2dec5bits, as the project stores it:
LIBRARY ieee;
USE ieee.std_logic_1164.all;

ENTITY meu_bin2dec5bits IS
  PORT (
  	--entrada do binario de 5 bits
  	BIN_4, BIN_3, BIN_2, BIN_1, BIN_0: IN std_logic;

  	--saídas dos displays
  	S_a0, S_b0, S_c0, S_d0, S_e0, S_f0, S_g0: OUT std_logic; --display da unidade
  	S_a1, S_b1, S_c1, S_d1, S_e1, S_f1, S_g1: OUT std_logic  --display da dezena
    );
END meu_bin2dec5bits;

ARCHITECTURE TypeArchitecture OF meu_bin2dec5bits IS
    signal a1, b1, c1, d1: std_logic; --auxiliares
    signal e1, f1, g1, h1: std_logic; --auxiliares 
BEGIN
	process(BIN_4, BIN_3, BIN_2, BIN_1, BIN_0) is
		variable BIN_org: std_logic_vector(4 DOWNTO 0);
    		variable BCD0_org, BCD1_org: std_logic_vector(3 DOWNTO 0);
    		
    		variable BIN_shf: std_logic_vector(4 DOWNTO 0);
    		variable BCD0_shf, BCD1_shf: std_logic_vector(3 DOWNTO 0);
    		
    		variable a, b, c, d: std_logic;
    		variable e, f, g, h: std_logic;
	begin
		BIN_org(4) := BIN_4; BIN_org(3) := BIN_3;
		BIN_org(2) := BIN_2; BIN_org(1) := BIN_1;
		BIN_org(0) := BIN_0;
		
		BCD0_org := "0000";
		BCD1_org := "0000";
		for i in 4 downto 0 loop
			a := BCD0_org(3); b := BCD0_org(2);
			c := BCD0_org(1); d := BCD0_org(0);
			
			e := BCD1_org(3); f := BCD1_org(2);
			g := BCD1_org(1); h := BCD1_org(0);
			
		   	--somar 3 quando maior que 5
		   	BCD0_shf(3) := ((b and d) or (b and c)) or a;
		   	BCD0_shf(2) := (b and not c and not d) or (a and d) or (a and c);
		   	BCD0_shf(1) := (not a and not b and c) or (c and d) or (a and not c and not d) or (a and b and not d);
		   	BCD0_shf(0) := (not a and not b and d) or (not a and b and c and not d) or (a and not b and not d) or (a and b and d) or (a and not c and not d);
				
			BCD1_shf(3) := (f and h) or (f and g) or e;
		   	BCD1_shf(2) := (f and not g and not h) or (e and h) or (e and g);
		   	BCD1_shf(1) := (not e and not f and g) or (g and h) or (e and not g and not h) or (e and f and not h);
		   	BCD1_shf(0) := (not e and not f and h) or (not e and f and g and not h) or (e and not f and not h) or (e and f and h) or (e and not g and not h);
			
			BCD0_org := BCD0_shf;
			BCD1_org := BCD1_shf;
			
			--mudar primeira celula do bcd
			BCD1_shf(3) := BCD1_org(2);
			BCD1_shf(2) := BCD1_org(1);
			BCD1_shf(1) := BCD1_org(0);
			BCD1_shf(0) := BCD0_org(3);
			
			--mudar segunda celula do bcd
			BCD0_shf(3) := BCD0_org(2);
			BCD0_shf(2) := BCD0_org(1);
			BCD0_shf(1) := BCD0_org(0);
			BCD0_shf(0) := BIN_org(4);
			
			--mudar o binario
			BIN_shf(4) := BIN_org(3);
			BIN_shf(3) := BIN_org(2);
			BIN_shf(2) := BIN_org(1);
			BIN_shf(1) := BIN_org(0);
			BIN_shf(0) := '0';
			
			BIN_org := BIN_shf;
			BCD0_org := BCD0_shf;
			BCD1_org := BCD1_shf;
		 end loop;
		 
		--Bits do bcd da unidade
		a1 <= BCD0_org(3); b1 <= BCD0_org(2);
		c1 <= BCD0_org(1); d1 <= BCD0_org(0);
		
		--Bits do bcd da dezena
		e1 <= BCD1_org(3); f1 <= BCD1_org(2);
		g1 <= BCD1_org(1); h1 <= BCD1_org(0);
	end process;
	
	--Primeiro display
	S_a0 <= a1 or c1 or not ((not b1 and d1) or (b1 and not d1));
	
	S_b0 <= not b1 or not ((not c1 and d1) or (c1 and not d1));
	
	S_c0 <= b1 or not c1 or d1;
	
	S_d0 <= a1 or 
		(not b1 and not d1) or
		(not b1 and c1) or
		(c1 and not d1) or
		(b1 and not c1 and d1);

	S_e0 <= (not b1 and not d1) or
		(c1 and not d1);

	S_f0 <= a1 or
		(not c1 and not d1) or
		(b1 and not c1) or
		(b1 and not d1);

	S_g0 <= a1 or
		((not b1 and c1) or (b1 and not c1)) or
		(c1 and not d1);

	--Segundo display
	S_a1 <= e1 or g1 or not ((not f1 and h1) or (f1 and not h1));
	
	S_b1 <= not f1 or not ((not g1 and h1) or (g1 and not h1));
	
	S_c1 <= f1 or not g1 or h1;
	
	S_d1 <= e1 or 
		(not f1 and not h1) or
		(not f1 and g1) or
		(g1 and not h1) or
		(f1 and not g1 and h1);

	S_e1 <= (not f1 and not h1) or
		(g1 and not h1);

	S_f1 <= e1 or
		(not g1 and not h1) or
		(f1 and not g1) or
		(f1 and not h1);

	S_g1 <= e1 or
		((not g1 and f1) or (g1 and not f1)) or
		(g1 and not h1);
	
END TypeArchitecture;

// VHDL entity meu_bcd2dec, as the project stores it:
LIBRARY ieee;
USE ieee.std_logic_1164.all;

ENTITY meu_bcd2dec IS
  PORT (
  	BCD: IN std_logic_vector(3 downto 0);
  	a, b, c, d, e, f, g, h: OUT std_logic
    );
END meu_bcd2dec;

ARCHITECTURE TypeArchitecture OF meu_bcd2dec IS
    signal A, B, C, D: std_logic;
BEGIN
	A <= BCD(3); B <= BCD(2);
	C <= BCD(1); D <= BCD(0);
	
	--Primeiro display
	a <= A or C or not (B xor D);
	
	b <= not B or not (C xor D);
	
	c <= B or not C or D;
	
	d <= A or 
		(not B and not D) or
		(not B and C) or
		(C and not D) or
		(B and not C and D);

	e <= (not B and not D) or
		(C and not D);

	f <= A or
		(not C and not D) or
		(B and not C) or
		(B and not D);

	g <= A or
		(B xor C) or
		(C and not D);
	
END TypeArchitecture;
