// Logisim project somador_pl.circ as structural Verilog: 10 circuits, main circuit main
module main (
  input  A0,
  input  A1,
  input  A2,
  input  A3,
  input  A4,
  input  A5,
  input  A6,
  input  A7,
  input  A8,
  input  A9,
  input  B0,
  input  B1,
  input  B2,
  input  B3,
  input  B4,
  input  B5,
  input  B6,
  input  B7,
  input  B8,
  input  B9
);

  wire d1, d2, d3, d4, d5, d6, d7, u1, u2, u3, u4, u5, u6, u7;

  _7_Segment_Display u_7_segment_display_1 (.g(d7), .f(d6), .a(d1), .b(d2), .e(d5), .d(d4), .c(d3));  // open: dp
  somador_pl somador_pl_1 (
    .A0(A0), .A1(A1), .A2(A2), .A3(A3), .A4(A4), .A5(A5), .A6(A6), .A7(A7), .A8(A8), .A9(A9), .B0(B0),
    .B1(B1), .B2(B2), .B3(B3), .B4(B4), .B5(B5), .B6(B6), .B7(B7), .B8(B8), .B9(B9), .d1(d1), .d2(d2),
    .d3(d3), .d4(d4), .d5(d5), .d6(d6), .d7(d7), .u1(u1), .u2(u2), .u3(u3), .u4(u4), .u5(u5), .u6(u6), .u7(u7));
  _7_Segment_Display u_7_segment_display_2 (.g(u7), .f(u6), .a(u1), .b(u2), .e(u5), .d(u4), .c(u3));  // open: dp

  // Notes on the sheet:
  //   Portas Lógicas
  //   Portas Lógicas
endmodule

module soma1bit (
  input  Carry_ant,
  input  A,
  input  B,
  output Soma,
  output Carry
);

  wire meio_somador_1_s_soma, meio_somador_1_t_soma, meio_somador_2_t_soma;

  meio_somador meio_somador_1 (.A(A), .B(Carry_ant), .S_soma(meio_somador_1_s_soma), .T_soma(meio_somador_1_t_soma));
  meio_somador meio_somador_2 (.A(meio_somador_1_s_soma), .B(B), .S_soma(Soma), .T_soma(meio_somador_2_t_soma));
  or or_1 (Carry, meio_somador_1_t_soma, meio_somador_2_t_soma);
endmodule

module soma4bits (
  input  A3,
  input  A2,
  input  A1,
  input  A0,
  input  B3,
  input  B2,
  input  B1,
  input  B0,
  output S_0,
  output S_1,
  output S_2,
  output S_3,
  output S_overflow
);

  wire soma1bit_1_carry, soma1bit_2_carry, soma1bit_3_carry;

  soma1bit soma1bit_1 (.Carry_ant(1'b0), .A(A0), .B(B0), .Soma(S_0), .Carry(soma1bit_1_carry));
  soma1bit soma1bit_2 (.Carry_ant(soma1bit_1_carry), .A(A1), .B(B1), .Soma(S_1), .Carry(soma1bit_2_carry));
  soma1bit soma1bit_3 (.Carry_ant(soma1bit_2_carry), .A(A2), .B(B2), .Soma(S_2), .Carry(soma1bit_3_carry));
  soma1bit soma1bit_4 (.Carry_ant(soma1bit_3_carry), .A(A3), .B(B3), .Soma(S_3), .Carry(S_overflow));
endmodule

module meio_somador (
  input  A,
  input  B,
  output S_soma,
  output T_soma
);

  wire and_1_out, and_2_out, not_1_out, not_2_out;

  not not_1 (not_1_out, A);
  not not_2 (not_2_out, B);
  and and_1 (and_1_out, not_1_out, B);
  and and_2 (and_2_out, A, not_2_out);
  and and_3 (T_soma, A, B);
  or or_1 (S_soma, and_1_out, and_2_out);
endmodule

module Dec2Bin_4bits (
  input  A0,
  input  A1,
  input  A2,
  input  A3,
  input  A4,
  input  A5,
  input  A6,
  input  A7,
  input  A8,
  input  A9,
  output b0,
  output b1,
  output b2,
  output b3
);

  or or_1 (b3, A9, A8);
  or or_2 (b2, A4, A5, A6, A7);
  or or_3 (b1, A2, A3, A6, A7);
  or or_4 (b0, A7, A1, A3, A5, A9);
endmodule

module Bin2Dec_7Seg_5bits (
  input  b4,
  input  b3,
  input  b2,
  input  b1,
  input  b0,
  output d1,
  output d2,
  output d3,
  output d4,
  output d5,
  output d6,
  output d7,
  output u1,
  output u2,
  output u3,
  output u4,
  output u5,
  output u6,
  output u7
);

  wire bloco_desena_1_w, bloco_desena_1_x, bloco_desena_1_y, bloco_desena_1_z, bloco_unidade_1_w,
       bloco_unidade_1_x, bloco_unidade_1_y, bloco_unidade_1_z;

  bloco_desena bloco_desena_1 (
    .a(b4), .b(b3), .c(b2), .d(b1), .e(b0), .w(bloco_desena_1_w), .x(bloco_desena_1_x), .y(bloco_desena_1_y),
    .z(bloco_desena_1_z));
  bloco_unidade bloco_unidade_1 (
    .a(b4), .b(b3), .c(b2), .d(b1), .e(b0), .w(bloco_unidade_1_w), .x(bloco_unidade_1_x),
    .y(bloco_unidade_1_y), .z(bloco_unidade_1_z));
  codificador7seguimeto codificador7seguimeto_1 (
    .a(bloco_desena_1_w), .b(bloco_desena_1_x), .c(bloco_desena_1_y), .d(bloco_desena_1_z), .s1(d1), .s2(d2),
    .s3(d3), .s4(d4), .s5(d5), .s6(d6), .s7(d7));
  codificador7seguimeto codificador7seguimeto_2 (
    .a(bloco_unidade_1_w), .b(bloco_unidade_1_x), .c(bloco_unidade_1_y), .d(bloco_unidade_1_z), .s1(u1),
    .s2(u2), .s3(u3), .s4(u4), .s5(u5), .s6(u6), .s7(u7));
endmodule

module codificador7seguimeto (
  input  a,
  input  b,
  input  c,
  input  d,
  output s1,
  output s2,
  output s3,
  output s4,
  output s5,
  output s6,
  output s7
);

  wire and_1_out, and_2_out, and_3_out, and_4_out, and_5_out, and_6_out, and_7_out, and_8_out, and_9_out,
       and_10_out, and_11_out, and_12_out, and_13_out, and_14_out, and_15_out, and_16_out, and_17_out,
       and_18_out, and_19_out, and_20_out, and_21_out, and_22_out, and_23_out, and_24_out, and_25_out,
       and_26_out, and_27_out, not_1_out, not_2_out, not_3_out, not_4_out;

  not not_1 (not_1_out, a);
  not not_2 (not_2_out, b);
  not not_3 (not_3_out, c);
  not not_4 (not_4_out, d);
  and and_1 (and_1_out, not_2_out, not_4_out);
  and and_2 (and_2_out, b, d);
  and and_3 (and_3_out, not_1_out, not_2_out);
  and and_4 (and_4_out, not_3_out, not_4_out);
  and and_5 (and_5_out, not_1_out, c, d);
  and and_6 (and_6_out, not_2_out, d);
  and and_7 (and_7_out, a, not_3_out);
  and and_8 (and_8_out, a, b, not_4_out);
  and and_9 (and_9_out, not_1_out, d);
  and and_10 (and_10_out, not_3_out, d);
  and and_11 (and_11_out, not_1_out, b);
  and and_12 (and_12_out, not_2_out, not_3_out);
  and and_13 (and_13_out, a, c, not_4_out);
  and and_14 (and_14_out, not_2_out, not_4_out);
  and and_15 (and_15_out, not_1_out, not_2_out, c);
  and and_16 (and_16_out, not_1_out, b, not_3_out, d);
  and and_17 (and_17_out, c, not_4_out);
  and and_18 (and_18_out, a, not_2_out, not_3_out);
  and and_19 (and_19_out, a, not_4_out);
  and and_20 (and_20_out, not_2_out, not_4_out);
  and and_21 (and_21_out, c, not_4_out);
  and and_22 (and_22_out, not_3_out, not_4_out);
  and and_23 (and_23_out, b, not_3_out);
  and and_24 (and_24_out, b, not_4_out);
  and and_25 (and_25_out, not_2_out, c);
  and and_26 (and_26_out, b, not_3_out);
  and and_27 (and_27_out, c, not_4_out);
  or or_1 (s1, and_1_out, c, and_2_out, a);
  or or_2 (s2, and_3_out, and_4_out, and_5_out, and_6_out, and_7_out, and_8_out);
  or or_3 (s3, and_9_out, and_10_out, and_11_out, and_12_out, and_13_out);
  or or_4 (s4, and_14_out, and_15_out, and_16_out, and_17_out, and_18_out, and_19_out);
  or or_5 (s5, and_20_out, and_21_out);
  or or_6 (s6, and_22_out, and_23_out, and_24_out, a);
  or or_7 (s7, and_25_out, and_26_out, a, and_27_out);
endmodule

module bloco_desena (
  input  a,
  input  b,
  input  c,
  input  d,
  input  e,
  output w,
  output x,
  output y,
  output z
);

  wire and_1_out, and_2_out, and_3_out, and_4_out, and_5_out, and_6_out, not_1_out, not_2_out, not_3_out;

  not not_1 (not_1_out, a);
  not not_2 (not_2_out, b);
  not not_3 (not_3_out, c);
  and and_1 (and_1_out, a, c);
  and and_2 (and_2_out, a, b);
  and and_3 (and_3_out, a, not_2_out, not_3_out);
  and and_4 (and_4_out, not_1_out, b, d);
  and and_5 (and_5_out, not_1_out, b, c);
  and and_6 (and_6_out, b, c, d);
  or or_1 (y, and_1_out, and_2_out);
  or or_2 (z, and_3_out, and_4_out, and_5_out, and_6_out);

  assign w = 1'b0;
  assign x = 1'b0;
endmodule

module bloco_unidade (
  input  a,
  input  b,
  input  c,
  input  d,
  input  e,
  output w,
  output x,
  output y,
  output z
);

  wire and_1_out, and_2_out, and_3_out, and_4_out, and_5_out, and_6_out, and_7_out, and_8_out, and_9_out,
       and_10_out, and_11_out, and_12_out, not_1_out, not_2_out, not_3_out, not_4_out;

  not not_1 (not_1_out, a);
  not not_2 (not_2_out, b);
  not not_3 (not_3_out, c);
  not not_4 (not_4_out, d);
  and and_1 (and_1_out, a, not_2_out, not_3_out, d);
  and and_2 (and_2_out, not_1_out, b, not_3_out, not_4_out);
  and and_3 (and_3_out, a, b, c, not_4_out);
  and and_4 (and_4_out, a, not_3_out, not_4_out);
  and and_5 (and_5_out, not_1_out, not_2_out, c);
  and and_6 (and_6_out, a, b, not_3_out);
  and and_7 (and_7_out, not_1_out, c, d);
  and and_8 (and_8_out, a, not_2_out, not_3_out, not_4_out);
  and and_9 (and_9_out, not_1_out, not_2_out, d);
  and and_10 (and_10_out, not_2_out, c, d);
  and and_11 (and_11_out, a, b, not_3_out, d);
  and and_12 (and_12_out, not_1_out, b, c, not_4_out);
  or or_1 (w, and_1_out, and_2_out, and_3_out);
  or or_2 (x, and_4_out, and_5_out, and_6_out, and_7_out);
  or or_3 (y, and_8_out, and_9_out, and_10_out, and_11_out, and_12_out);

  assign z = e;
endmodule

module somador_pl (
  input  A0,
  input  A1,
  input  A2,
  input  A3,
  input  A4,
  input  A5,
  input  A6,
  input  A7,
  input  A8,
  input  A9,
  input  B0,
  input  B1,
  input  B2,
  input  B3,
  input  B4,
  input  B5,
  input  B6,
  input  B7,
  input  B8,
  input  B9,
  output d1,
  output d2,
  output d3,
  output d4,
  output d5,
  output d6,
  output d7,
  output u1,
  output u2,
  output u3,
  output u4,
  output u5,
  output u6,
  output u7
);

  wire dec2bin_4bits_1_b0, dec2bin_4bits_1_b1, dec2bin_4bits_1_b2, dec2bin_4bits_1_b3, dec2bin_4bits_2_b0,
       dec2bin_4bits_2_b1, dec2bin_4bits_2_b2, dec2bin_4bits_2_b3, soma4bits_1_s_0, soma4bits_1_s_1,
       soma4bits_1_s_2, soma4bits_1_s_3, soma4bits_1_s_overflow;

  Dec2Bin_4bits dec2bin_4bits_1 (
    .A0(A0), .A1(A1), .A2(A2), .A3(A3), .A4(A4), .A5(A5), .A6(A6), .A7(A7), .A8(A8), .A9(A9),
    .b0(dec2bin_4bits_1_b0), .b1(dec2bin_4bits_1_b1), .b2(dec2bin_4bits_1_b2), .b3(dec2bin_4bits_1_b3));
  Dec2Bin_4bits dec2bin_4bits_2 (
    .A0(B0), .A1(B1), .A2(B2), .A3(B3), .A4(B4), .A5(B5), .A6(B6), .A7(B7), .A8(B8), .A9(B9),
    .b0(dec2bin_4bits_2_b0), .b1(dec2bin_4bits_2_b1), .b2(dec2bin_4bits_2_b2), .b3(dec2bin_4bits_2_b3));
  soma4bits soma4bits_1 (
    .A3(dec2bin_4bits_1_b3), .A2(dec2bin_4bits_1_b2), .A1(dec2bin_4bits_1_b1), .A0(dec2bin_4bits_1_b0),
    .B3(dec2bin_4bits_2_b3), .B2(dec2bin_4bits_2_b2), .B1(dec2bin_4bits_2_b1), .B0(dec2bin_4bits_2_b0),
    .S_0(soma4bits_1_s_0), .S_1(soma4bits_1_s_1), .S_2(soma4bits_1_s_2), .S_3(soma4bits_1_s_3),
    .S_overflow(soma4bits_1_s_overflow));
  Bin2Dec_7Seg_5bits bin2dec_7seg_5bits_1 (
    .b4(soma4bits_1_s_overflow), .b3(soma4bits_1_s_3), .b2(soma4bits_1_s_2), .b1(soma4bits_1_s_1),
    .b0(soma4bits_1_s_0), .d1(d1), .d2(d2), .d3(d3), .d4(d4), .d5(d5), .d6(d6), .d7(d7), .u1(u1), .u2(u2),
    .u3(u3), .u4(u4), .u5(u5), .u6(u6), .u7(u7));
endmodule
