// Logisim project trabalho2.circ as structural Verilog
module main (
  input  A0,
  input  A1,
  input  A2,
  input  A3,
  input  A4,
  input  A5,
  input  A6,
  input  A7,
  input  A8,
  input  A9,
  input  B0,
  input  B1,
  input  B2,
  input  B3,
  input  B4,
  input  B5,
  input  B6,
  input  B7,
  input  B8,
  input  B9
);

  wire d01, d1, d02, d2, d03, d3, d04, d4, d05, d5, d06, d6, d07, d7, d11, d12, d13, d14, d15, d16, d17, u01,
       u1, u02, u2, u03, u3, u04, u4, u05, u5, u06, u6, u07, u7, u11, u12, u13, u14, u15, u16, u17;

  somador_pl somador_pl_1 (
    .A0(A0), .A1(A1), .A2(A2), .A3(A3), .A4(A4), .A5(A5), .A6(A6), .A7(A7), .A8(A8), .A9(A9), .B0(B0),
    .B1(B1), .B2(B2), .B3(B3), .B4(B4), .B5(B5), .B6(B6), .B7(B7), .B8(B8), .B9(B9), .d1(d1), .d2(d2),
    .d3(d3), .d4(d4), .d5(d5), .d6(d6), .d7(d7), .u1(u1), .u2(u2), .u3(u3), .u4(u4), .u5(u5), .u6(u6), .u7(u7));
  _7_Segment_Display u_7_segment_display_1 (.g(d7), .f(d6), .a(d1), .b(d2), .e(d5), .d(d4), .c(d3));  // open: dp
  _7_Segment_Display u_7_segment_display_2 (.g(u7), .f(u6), .a(u1), .b(u2), .e(u5), .d(u4), .c(u3));  // open: dp
  _7_Segment_Display u_7_segment_display_3 (.g(d07), .f(d06), .a(d01), .b(d02), .e(d05), .d(d04), .c(d03));  // open: dp
  somador_vhdl somador_vhdl_1 (
    .a0(A0), .a1(A1), .a2(A2), .a3(A3), .a4(A4), .a5(A5), .a6(A6), .a7(A7), .a8(A8), .a9(A9), .b0(B0),
    .b1(B1), .b2(B2), .b3(B3), .b4(B4), .b5(B5), .b6(B6), .b7(B7), .b8(B8), .b9(B9), .S_a0(u01), .S_b0(u02),
    .S_c0(u03), .S_d0(u04), .S_e0(u05), .S_f0(u06), .S_g0(u07), .S_a1(d01), .S_b1(d02), .S_c1(d03),
    .S_d1(d04), .S_e1(d05), .S_f1(d06), .S_g1(d07));
  _7_Segment_Display u_7_segment_display_4 (.g(u07), .f(u06), .a(u01), .b(u02), .e(u05), .d(u04), .c(u03));  // open: dp
  _7_Segment_Display u_7_segment_display_5 (.g(d17), .f(d16), .a(d11), .b(d12), .e(d15), .d(d14), .c(d13));  // open: dp
  _7_Segment_Display u_7_segment_display_6 (.g(u17), .f(u16), .a(u11), .b(u12), .e(u15), .d(u14), .c(u13));  // open: dp

  // Notes on the sheet:
  //   Portas Lógicas
  //   Portas Lógicas
  //   VHDL
  //   VHDL
  //   Circuito Integrado
  //   Circuito Integrado
endmodule

module meio_somador (
  input  A,
  input  B,
  output S_soma,
  output T_soma
);

  wire and_1_out, and_2_out, not_1_out, not_2_out;

  not not_1 (not_1_out, A);
  not not_2 (not_2_out, B);
  and and_1 (and_1_out, not_1_out, B);
  and and_2 (and_2_out, A, not_2_out);
  and and_3 (T_soma, A, B);
  or or_1 (S_soma, and_1_out, and_2_out);
endmodule

module soma1bit (
  input  Carry_ant,
  input  A,
  input  B,
  output Soma,
  output Carry
);

  wire meio_somador_1_s_soma, meio_somador_1_t_soma, meio_somador_2_t_soma;

  meio_somador meio_somador_1 (.A(A), .B(Carry_ant), .S_soma(meio_somador_1_s_soma), .T_soma(meio_somador_1_t_soma));
  meio_somador meio_somador_2 (.A(meio_somador_1_s_soma), .B(B), .S_soma(Soma), .T_soma(meio_somador_2_t_soma));
  or or_1 (Carry, meio_somador_1_t_soma, meio_somador_2_t_soma);
endmodule

module soma4bits (
  input  A3,
  input  A2,
  input  A1,
  input  A0,
  input  B3,
  input  B2,
  input  B1,
  input  B0,
  output S_0,
  output S_1,
  output S_2,
  output S_3,
  output S_overflow
);

  wire soma1bit_1_carry, soma1bit_2_carry, soma1bit_3_carry;

  soma1bit soma1bit_1 (.Carry_ant(1'b0), .A(A0), .B(B0), .Soma(S_0), .Carry(soma1bit_1_carry));
  soma1bit soma1bit_2 (.Carry_ant(soma1bit_1_carry), .A(A1), .B(B1), .Soma(S_1), .Carry(soma1bit_2_carry));
  soma1bit soma1bit_3 (.Carry_ant(soma1bit_2_carry), .A(A2), .B(B2), .Soma(S_2), .Carry(soma1bit_3_carry));
  soma1bit soma1bit_4 (.Carry_ant(soma1bit_3_carry), .A(A3), .B(B3), .Soma(S_3), .Carry(S_overflow));
endmodule

module Dec2Bin_4bits (
  input  A0,
  input  A1,
  input  A2,
  input  A3,
  input  A4,
  input  A5,
  input  A6,
  input  A7,
  input  A8,
  input  A9,
  output b0,
  output b1,
  output b2,
  output b3
);

  or or_1 (b3, A9, A8);
  or or_2 (b2, A4, A5, A6, A7);
  or or_3 (b1, A2, A3, A6, A7);
  or or_4 (b0, A7, A1, A3, A5, A9);
endmodule

module Bin2Dec_7Seg_5bits (
  input  b4,
  input  b3,
  input  b2,
  input  b1,
  input  b0,
  output d1,
  output d2,
  output d3,
  output d4,
  output d5,
  output d6,
  output d7,
  output u1,
  output u2,
  output u3,
  output u4,
  output u5,
  output u6,
  output u7
);

  wire bloco_desena_1_w, bloco_desena_1_x, bloco_desena_1_y, bloco_desena_1_z, bloco_unidade_1_w,
       bloco_unidade_1_x, bloco_unidade_1_y, bloco_unidade_1_z;

  bloco_desena bloco_desena_1 (
    .a(b4), .b(b3), .c(b2), .d(b1), .e(b0), .w(bloco_desena_1_w), .x(bloco_desena_1_x), .y(bloco_desena_1_y),
    .z(bloco_desena_1_z));
  bloco_unidade bloco_unidade_1 (
    .a(b4), .b(b3), .c(b2), .d(b1), .e(b0), .w(bloco_unidade_1_w), .x(bloco_unidade_1_x),
    .y(bloco_unidade_1_y), .z(bloco_unidade_1_z));
  codificador7seguimeto codificador7seguimeto_1 (
    .a(bloco_desena_1_w), .b(bloco_desena_1_x), .c(bloco_desena_1_y), .d(bloco_desena_1_z), .s1(d1), .s2(d2),
    .s3(d3), .s4(d4), .s5(d5), .s6(d6), .s7(d7));
  codificador7seguimeto codificador7seguimeto_2 (
    .a(bloco_unidade_1_w), .b(bloco_unidade_1_x), .c(bloco_unidade_1_y), .d(bloco_unidade_1_z), .s1(u1),
    .s2(u2), .s3(u3), .s4(u4), .s5(u5), .s6(u6), .s7(u7));
endmodule

module codificador7seguimeto (
  input  a,
  input  b,
  input  c,
  input  d,
  output s1,
  output s2,
  output s3,
  output s4,
  output s5,
  output s6,
  output s7
);

  wire and_1_out, and_2_out, and_3_out, and_4_out, and_5_out, and_6_out, and_7_out, and_8_out, and_9_out,
       and_10_out, and_11_out, and_12_out, and_13_out, and_14_out, and_15_out, and_16_out, and_17_out,
       and_18_out, and_19_out, and_20_out, and_21_out, and_22_out, and_23_out, and_24_out, and_25_out,
       and_26_out, and_27_out, not_1_out, not_2_out, not_3_out, not_4_out;

  not not_1 (not_1_out, a);
  not not_2 (not_2_out, b);
  not not_3 (not_3_out, c);
  not not_4 (not_4_out, d);
  and and_1 (and_1_out, not_2_out, not_4_out);
  and and_2 (and_2_out, b, d);
  and and_3 (and_3_out, not_1_out, not_2_out);
  and and_4 (and_4_out, not_3_out, not_4_out);
  and and_5 (and_5_out, not_1_out, c, d);
  and and_6 (and_6_out, not_2_out, d);
  and and_7 (and_7_out, a, not_3_out);
  and and_8 (and_8_out, a, b, not_4_out);
  and and_9 (and_9_out, not_1_out, d);
  and and_10 (and_10_out, not_3_out, d);
  and and_11 (and_11_out, not_1_out, b);
  and and_12 (and_12_out, not_2_out, not_3_out);
  and and_13 (and_13_out, a, c, not_4_out);
  and and_14 (and_14_out, not_2_out, not_4_out);
  and and_15 (and_15_out, not_1_out, not_2_out, c);
  and and_16 (and_16_out, not_1_out, b, not_3_out, d);
  and and_17 (and_17_out, c, not_4_out);
  and and_18 (and_18_out, a, not_2_out, not_3_out);
  and and_19 (and_19_out, a, not_4_out);
  and and_20 (and_20_out, not_2_out, not_4_out);
  and and_21 (and_21_out, c, not_4_out);
  and and_22 (and_22_out, not_3_out, not_4_out);
  and and_23 (and_23_out, b, not_3_out);
  and and_24 (and_24_out, b, not_4_out);
  and and_25 (and_25_out, not_2_out, c);
  and and_26 (and_26_out, b, not_3_out);
  and and_27 (and_27_out, c, not_4_out);
  or or_1 (s1, and_1_out, c, and_2_out, a);
  or or_2 (s2, and_3_out, and_4_out, and_5_out, and_6_out, and_7_out, and_8_out);
  or or_3 (s3, and_9_out, and_10_out, and_11_out, and_12_out, and_13_out);
  or or_4 (s4, and_14_out, and_15_out, and_16_out, and_17_out, and_18_out, and_19_out);
  or or_5 (s5, and_20_out, and_21_out);
  or or_6 (s6, and_22_out, and_23_out, and_24_out, a);
  or or_7 (s7, and_25_out, and_26_out, a, and_27_out);
endmodule

module bloco_desena (
  input  a,
  input  b,
  input  c,
  input  d,
  input  e,
  output w,
  output x,
  output y,
  output z
);

  wire and_1_out, and_2_out, and_3_out, and_4_out, and_5_out, and_6_out, not_1_out, not_2_out, not_3_out;

  not not_1 (not_1_out, a);
  not not_2 (not_2_out, b);
  not not_3 (not_3_out, c);
  and and_1 (and_1_out, a, c);
  and and_2 (and_2_out, a, b);
  and and_3 (and_3_out, a, not_2_out, not_3_out);
  and and_4 (and_4_out, not_1_out, b, d);
  and and_5 (and_5_out, not_1_out, b, c);
  and and_6 (and_6_out, b, c, d);
  or or_1 (y, and_1_out, and_2_out);
  or or_2 (z, and_3_out, and_4_out, and_5_out, and_6_out);

  assign w = 1'b0;
  assign x = 1'b0;
endmodule

module bloco_unidade (
  input  a,
  input  b,
  input  c,
  input  d,
  input  e,
  output w,
  output x,
  output y,
  output z
);

  wire and_1_out, and_2_out, and_3_out, and_4_out, and_5_out, and_6_out, and_7_out, and_8_out, and_9_out,
       and_10_out, and_11_out, and_12_out, not_1_out, not_2_out, not_3_out, not_4_out;

  not not_1 (not_1_out, a);
  not not_2 (not_2_out, b);
  not not_3 (not_3_out, c);
  not not_4 (not_4_out, d);
  and and_1 (and_1_out, a, not_2_out, not_3_out, d);
  and and_2 (and_2_out, not_1_out, b, not_3_out, not_4_out);
  and and_3 (and_3_out, a, b, c, not_4_out);
  and and_4 (and_4_out, a, not_3_out, not_4_out);
  and and_5 (and_5_out, not_1_out, not_2_out, c);
  and and_6 (and_6_out, a, b, not_3_out);
  and and_7 (and_7_out, not_1_out, c, d);
  and and_8 (and_8_out, a, not_2_out, not_3_out, not_4_out);
  and and_9 (and_9_out, not_1_out, not_2_out, d);
  and and_10 (and_10_out, not_2_out, c, d);
  and and_11 (and_11_out, a, b, not_3_out, d);
  and and_12 (and_12_out, not_1_out, b, c, not_4_out);
  or or_1 (w, and_1_out, and_2_out, and_3_out);
  or or_2 (x, and_4_out, and_5_out, and_6_out, and_7_out);
  or or_3 (y, and_8_out, and_9_out, and_10_out, and_11_out, and_12_out);

  assign z = e;
endmodule

module somador_pl (
  input  A0,
  input  A1,
  input  A2,
  input  A3,
  input  A4,
  input  A5,
  input  A6,
  input  A7,
  input  A8,
  input  A9,
  input  B0,
  input  B1,
  input  B2,
  input  B3,
  input  B4,
  input  B5,
  input  B6,
  input  B7,
  input  B8,
  input  B9,
  output d1,
  output d2,
  output d3,
  output d4,
  output d5,
  output d6,
  output d7,
  output u1,
  output u2,
  output u3,
  output u4,
  output u5,
  output u6,
  output u7
);

  wire dec2bin_4bits_1_b0, dec2bin_4bits_1_b1, dec2bin_4bits_1_b2, dec2bin_4bits_1_b3, dec2bin_4bits_2_b0,
       dec2bin_4bits_2_b1, dec2bin_4bits_2_b2, dec2bin_4bits_2_b3, soma4bits_1_s_0, soma4bits_1_s_1,
       soma4bits_1_s_2, soma4bits_1_s_3, soma4bits_1_s_overflow;

  Dec2Bin_4bits dec2bin_4bits_1 (
    .A0(A0), .A1(A1), .A2(A2), .A3(A3), .A4(A4), .A5(A5), .A6(A6), .A7(A7), .A8(A8), .A9(A9),
    .b0(dec2bin_4bits_1_b0), .b1(dec2bin_4bits_1_b1), .b2(dec2bin_4bits_1_b2), .b3(dec2bin_4bits_1_b3));
  Dec2Bin_4bits dec2bin_4bits_2 (
    .A0(B0), .A1(B1), .A2(B2), .A3(B3), .A4(B4), .A5(B5), .A6(B6), .A7(B7), .A8(B8), .A9(B9),
    .b0(dec2bin_4bits_2_b0), .b1(dec2bin_4bits_2_b1), .b2(dec2bin_4bits_2_b2), .b3(dec2bin_4bits_2_b3));
  soma4bits soma4bits_1 (
    .A3(dec2bin_4bits_1_b3), .A2(dec2bin_4bits_1_b2), .A1(dec2bin_4bits_1_b1), .A0(dec2bin_4bits_1_b0),
    .B3(dec2bin_4bits_2_b3), .B2(dec2bin_4bits_2_b2), .B1(dec2bin_4bits_2_b1), .B0(dec2bin_4bits_2_b0),
    .S_0(soma4bits_1_s_0), .S_1(soma4bits_1_s_1), .S_2(soma4bits_1_s_2), .S_3(soma4bits_1_s_3),
    .S_overflow(soma4bits_1_s_overflow));
  Bin2Dec_7Seg_5bits bin2dec_7seg_5bits_1 (
    .b4(soma4bits_1_s_overflow), .b3(soma4bits_1_s_3), .b2(soma4bits_1_s_2), .b1(soma4bits_1_s_1),
    .b0(soma4bits_1_s_0), .d1(d1), .d2(d2), .d3(d3), .d4(d4), .d5(d5), .d6(d6), .d7(d7), .u1(u1), .u2(u2),
    .u3(u3), .u4(u4), .u5(u5), .u6(u6), .u7(u7));
endmodule

// VHDL entity somador_vhdl, as the project stores it:
LIBRARY ieee;
USE ieee.std_logic_1164.all;
USE ieee.numeric_std.all;

ENTITY somador_vhdl IS
  PORT (
    -- Entradas do 1º Número (Teclado A)
    a0, a1, a2, a3, a4, a5, a6, a7, a8, a9: IN std_logic;
    -- Entradas do 2º Número (Teclado B)
    b0, b1, b2, b3, b4, b5, b6, b7, b8, b9: IN std_logic;

    -- Saídas para o Display da Unidade
    S_a0, S_b0, S_c0, S_d0, S_e0, S_f0, S_g0: OUT std_logic;
    -- Saídas para o Display da Dezena
    S_a1, S_b1, S_c1, S_d1, S_e1, S_f1, S_g1: OUT std_logic
  );
END somador_vhdl;

ARCHITECTURE Comportamento OF somador_vhdl IS
    -- Fios internos para interligar os módulos dentro do código
    signal A_bin, B_bin : std_logic_vector(3 downto 0);
    signal Soma_bin : std_logic_vector(4 downto 0);
    
    signal a_uni, b_uni, c_uni, d_uni: std_logic; 
    signal e_dez, f_dez, g_dez, h_dez: std_logic; 
BEGIN
    -- ==========================================
    -- 1. CONVERSOR DEC2BIN (ENTRADAS A e B)
    -- ==========================================
    A_bin(3) <= a9 or a8;
    A_bin(2) <= a4 or a5 or a6 or a7;
    A_bin(1) <= a2 or a3 or a6 or a7;
    A_bin(0) <= a1 or a3 or a5 or a7 or a9;

    B_bin(3) <= b9 or b8;
    B_bin(2) <= b4 or b5 or b6 or b7;
    B_bin(1) <= b2 or b3 or b6 or b7;
    B_bin(0) <= b1 or b3 or b5 or b7 or b9;

    -- ==========================================
    -- 2. SOMADOR (A + B)
    -- ==========================================
    Soma_bin <= std_logic_vector(unsigned('0' & A_bin) + unsigned('0' & B_bin));

    -- ==========================================
    -- 3. CONVERSOR BIN2DEC (Shift-and-Add-3)
    -- ==========================================
    process(Soma_bin) is
        variable BIN_org: std_logic_vector(4 DOWNTO 0);
        variable BCD0_org, BCD1_org: std_logic_vector(3 DOWNTO 0);
        variable BIN_shf: std_logic_vector(4 DOWNTO 0);
        variable BCD0_shf, BCD1_shf: std_logic_vector(3 DOWNTO 0);
        variable a, b, c, d, e, f, g, h: std_logic;
    begin
        BIN_org := Soma_bin;
        BCD0_org := "0000";
        BCD1_org := "0000";
        
        for i in 4 downto 0 loop
            a := BCD0_org(3); b := BCD0_org(2);
            c := BCD0_org(1); d := BCD0_org(0);
            
            e := BCD1_org(3); f := BCD1_org(2);
            g := BCD1_org(1); h := BCD1_org(0);
            
            BCD0_shf(3) := ((b and d) or (b and c)) or a;
            BCD0_shf(2) := (b and not c and not d) or (a and d) or (a and c);
            BCD0_shf(1) := (not a and not b and c) or (c and d) or (a and not c and not d) or (a and b and not d);
            BCD0_shf(0) := (not a and not b and d) or (not a and b and c and not d) or (a and not b and not d) or (a and b and d) or (a and not c and not d);
                
            BCD1_shf(3) := (f and h) or (f and g) or e;
            BCD1_shf(2) := (f and not g and not h) or (e and h) or (e and g);
            BCD1_shf(1) := (not e and not f and g) or (g and h) or (e and not g and not h) or (e and f and not h);
            BCD1_shf(0) := (not e and not f and h) or (not e and f and g and not h) or (e and not f and not h) or (e and f and h) or (e and not g and not h);
            
            BCD0_org := BCD0_shf;
            BCD1_org := BCD1_shf;
            
            BCD1_shf(3) := BCD1_org(2);
            BCD1_shf(2) := BCD1_org(1);
            BCD1_shf(1) := BCD1_org(0);
            BCD1_shf(0) := BCD0_org(3);
            
            BCD0_shf(3) := BCD0_org(2);
            BCD0_shf(2) := BCD0_org(1);
            BCD0_shf(1) := BCD0_org(0);
            BCD0_shf(0) := BIN_org(4);
            
            BIN_shf(4) := BIN_org(3);
            BIN_shf(3) := BIN_org(2);
            BIN_shf(2) := BIN_org(1);
            BIN_shf(1) := BIN_org(0);
            BIN_shf(0) := '0';
            
            BIN_org := BIN_shf;
            BCD0_org := BCD0_shf;
            BCD1_org := BCD1_shf;
         end loop;
         
        a_uni <= BCD0_org(3); b_uni <= BCD0_org(2);
        c_uni <= BCD0_org(1); d_uni <= BCD0_org(0);
        
        e_dez <= BCD1_org(3); f_dez <= BCD1_org(2);
        g_dez <= BCD1_org(1); h_dez <= BCD1_org(0);
    end process;

    -- ==========================================
    -- 4. DECODIFICADORES 7-SEGMENTOS
    -- ==========================================
    S_a0 <= a_uni or c_uni or not ((not b_uni and d_uni) or (b_uni and not d_uni));
    S_b0 <= not b_uni or not ((not c_uni and d_uni) or (c_uni and not d_uni));
    S_c0 <= b_uni or not c_uni or d_uni;
    S_d0 <= a_uni or (not b_uni and not d_uni) or (not b_uni and c_uni) or (c_uni and not d_uni) or (b_uni and not c_uni and d_uni);
    S_e0 <= (not b_uni and not d_uni) or (c_uni and not d_uni);
    S_f0 <= a_uni or (not c_uni and not d_uni) or (b_uni and not c_uni) or (b_uni and not d_uni);
    S_g0 <= a_uni or ((not b_uni and c_uni) or (b_uni and not c_uni)) or (c_uni and not d_uni);

    S_a1 <= e_dez or g_dez or not ((not f_dez and h_dez) or (f_dez and not h_dez));
    S_b1 <= not f_dez or not ((not g_dez and h_dez) or (g_dez and not h_dez));
    S_c1 <= f_dez or not g_dez or h_dez;
    S_d1 <= e_dez or (not f_dez and not h_dez) or (not f_dez and g_dez) or (g_dez and not h_dez) or (f_dez and not g_dez and h_dez);
    S_e1 <= (not f_dez and not h_dez) or (g_dez and not h_dez);
    S_f1 <= e_dez or (not g_dez and not h_dez) or (f_dez and not g_dez) or (f_dez and not h_dez);
    S_g1 <= e_dez or ((not g_dez and f_dez) or (g_dez and not f_dez)) or (g_dez and not h_dez);

END Comportamento;
